# Fritzing sketch Teensy_3_Xbee (saved by Fritzing 0.7.11b)

parts:
  U1 = XBee
  Teensy_3_1 = Teensy 3.0 [part_number="Freescale ARM MK20DX128"]

nets:
  VCC: U1.VCC, Teensy_3_1.3.3V, Teensy_3_1.16, Teensy_3_1.15
  N1: U1.pin2, Teensy_3_1.7
  N2: U1.pin3, Teensy_3_1.8, Teensy_3_1.9
  GND: U1.GND, Teensy_3_1.GND, Teensy_3_1.0
