# Fritzing sketch rx (saved by Fritzing 0.9.3b)
circuit board: 8.46667cm x 5.64444cm
breadboards: 1

parts:
  HC-1 = HC-12 Module
  Antenna1 = HC-12 Antenna
  BAT1 = Battery Holders [part_number="DEVRAIT ETRE 5V" package=lipo-1100mAh]
  Teensy_3_1 = Teensy 3.0 [part_number="Freescale ARM MK20DX128"]
  KY-1 = Keyes Relay [part_number=RELAIS_1 package=THT]
  KY-2 = Keyes Relay [part_number=RELAIS_2 package=THT]
  USBTTL1 = USB TTL Serial Cable [part_number=CONFIG_INTERFACE]

nets (from the breadboard view):
  N1: HC-1.SET, Teensy_3_1.2
  N2: HC-1.TXD, Teensy_3_1.1
  N3: HC-1.RXD, Teensy_3_1.0
  N4: HC-1.GND, BAT1.-, Teensy_3_1.GND#22, KY-1.ground, KY-2.ground
  VCC: HC-1.VCC, BAT1.+, Teensy_3_1.Vin, KY-1.power, KY-2.power
  N5: HC-1.ANT, Antenna1.ANT
  N6: Teensy_3_1.AGND, Teensy_3_1.VUSB
  N7: Teensy_3_1.23, Teensy_3_1.AREF, KY-1.signal
  N8: Teensy_3_1.22, Teensy_3_1.A10, KY-2.signal
  N9: Teensy_3_1.21, Teensy_3_1.A11
  N10: Teensy_3_1.13, Teensy_3_1.Program, Teensy_3_1.RST
  N11: Teensy_3_1.9, USBTTL1.RX
  N12: Teensy_3_1.10, USBTTL1.TX
  N13: Teensy_3_1.12, Teensy_3_1.VBat

notes:
  J'ai pas trouvé de composant Fritzing pour une carte 2 relais.
  Les fils d'alim noirs et rouges sont donc en commun sur la carte qu'on a..

custom parts:
  HC-12 Module: HC-12 433Mhz Module
  HC-12 Antenna: Antenna for HC-12 433Mhz Module
  Keyes Relay: The Keyes 5V relay module is suitable for SCM development, home appliance control. It uses a 5V~12V TIL control signal which can control DC / AC signal.
