# Fritzing sketch tx (saved by Fritzing 0.9.3b)
circuit board: 8.46667cm x 5.64444cm
breadboards: 1

parts:
  HC-1 = HC-12 Module
  Antenna1 = HC-12 Antenna
  LED2 = LED - 3mm [color="Green (570nm)" part_number=LED_CONNECTION package="3 mm [THT]"]
  R6 = Resistor [tolerance=±5% resistance=220 package="2010 [SMD]"]
  LED1 = LED - 3mm [color="Red (633nm)" part_number=LED_RETOUR_MISE_A_FEU package="3 mm [THT]"]
  BAT1 = Battery Holders [part_number=ALIMENTATION package=lipo-1100mAh]
  S3 = Round Pushbutton [part_number=BOUTON_MISE_A_FEU]
  S4 = Toggle Switch [part_number=SWITCH_SELECTION_VALISE package=THT]
  S5 = Toggle Switch [part_number=SWITCH_SELECTION_RELAIS package=THT]
  R7 = Resistor [tolerance=±5% resistance=220 package="2010 [SMD]"]
  Teensy_3_1 = Teensy 3.0 [part_number="Freescale ARM MK20DX128"]
  USBTTL1 = USB TTL Serial Cable [part_number=CONFIG_INTERFACE]

nets (from the breadboard view):
  N1: HC-1.SET, Teensy_3_1.2
  N2: HC-1.TXD, Teensy_3_1.1
  N3: HC-1.RXD, Teensy_3_1.0
  N4: HC-1.GND, LED2.cathode, LED1.cathode, BAT1.-, S3.leg0, S4.COM, S5.COM, Teensy_3_1.GND#22
  VCC: HC-1.VCC, BAT1.+, Teensy_3_1.Vin
  N5: HC-1.ANT, Antenna1.ANT
  N6: R6.Pin_0, Teensy_3_1.3
  N7: S3.leg1, Teensy_3_1.12, Teensy_3_1.VBat
  N8: S4.L1, Teensy_3_1.23, Teensy_3_1.AREF
  N9: S5.L1, Teensy_3_1.22, Teensy_3_1.A10
  N10: R7.Pin_0, Teensy_3_1.4
  N11: Teensy_3_1.AGND, Teensy_3_1.VUSB
  N12: Teensy_3_1.21, Teensy_3_1.A11
  N13: Teensy_3_1.13, Teensy_3_1.Program, Teensy_3_1.RST
  N14: Teensy_3_1.9, USBTTL1.RX
  N15: Teensy_3_1.10, USBTTL1.TX

notes:
  La carte doit etre alimentee en 5V
  Tous les interrupteurs fonctionnent en INPUT_PULLUP, et donc leur valeur vaut HIGH quand en contact !
  Les sorties digitales de la carte sont en 3.3V, il faut donc choisir des valeurs de résistance en conséquence (selon le choix des LEDS)

custom parts:
  HC-12 Module: HC-12 433Mhz Module
  HC-12 Antenna: Antenna for HC-12 433Mhz Module
